// Logisim project seq_circuit.circ as structural Verilog: 1 circuit, main circuit main
module main (
  input  X,
  input  Y,
  output S
);

  wire and_1_out, and_2_out, d_ff_1_q, or_1_out, xor_1_out;

  xor xor_1 (xor_1_out, X, Y);
  and and_1 (and_1_out, X, Y);
  D_Flip_Flop d_ff_1 (.D(or_1_out), .Q(d_ff_1_q));  // open: clk, Qn, preset, en, reset
  xor xor_2 (S, xor_1_out, d_ff_1_q);
  and and_2 (and_2_out, xor_1_out, d_ff_1_q);
  or or_1 (or_1_out, and_2_out, and_1_out);
endmodule
